# Fritzing sketch shift_stepper_demo (saved by Fritzing 0.9.6b)
breadboards: 2

parts:
  IC1 = ULN2003A [package="DIP16 [THT]"]  # not connected
  IC2 = ULN2003A [package="DIP16 [THT]"]  # not connected
  U2 = 74HC595 [package="DIP16 [THT]"]
  U3 = 74HC595 [package="DIP16 [THT]"]
  LED1 = LED - 5mm [color="Red (633nm)" current=0.030 package="5 mm [THT]"]
  R1 = Resistor [tolerance=±5% power=0.25 resistance=220 package=THT]
  R2 = Resistor [tolerance=±5% power=0.25 resistance=220 package=THT]
  R3 = Resistor [tolerance=±5% power=0.25 resistance=220 package=THT]
  R4 = Resistor [tolerance=±5% power=0.25 resistance=220 package=THT]
  R5 = Resistor [tolerance=±5% power=0.25 resistance=220 package=THT]
  R6 = Resistor [tolerance=±5% power=0.25 resistance=220 package=THT]
  R7 = Resistor [tolerance=±5% power=0.25 resistance=220 package=THT]
  R8 = Resistor [tolerance=±5% power=0.25 resistance=220 package=THT]
  R9 = Resistor [tolerance=±5% power=0.25 resistance=220 package=THT]
  R10 = Resistor [tolerance=±5% power=0.25 resistance=220 package=THT]
  R11 = Resistor [tolerance=±5% power=0.25 resistance=220 package=THT]
  R12 = Resistor [tolerance=±5% power=0.25 resistance=220 package=THT]
  R13 = Resistor [tolerance=±5% power=0.25 resistance=220 package=THT]
  R14 = Resistor [tolerance=±5% power=0.25 resistance=220 package=THT]
  R15 = Resistor [tolerance=±5% power=0.25 resistance=220 package=THT]
  R16 = Resistor [tolerance=±5% power=0.25 resistance=220 package=THT]
  LED2 = LED - 5mm [color="Red (633nm)" current=0.030 package="5 mm [THT]"]
  LED3 = LED - 5mm [color="Red (633nm)" current=0.030 package="5 mm [THT]"]
  LED4 = LED - 5mm [color="Red (633nm)" current=0.030 package="5 mm [THT]"]
  LED5 = LED - 5mm [color="Orange (620nm)" current=0.030 package="5 mm [THT]"]
  LED6 = LED - 5mm [color="Orange (620nm)" current=0.030 package="5 mm [THT]"]
  LED7 = LED - 5mm [color="Orange (620nm)" current=0.030 package="5 mm [THT]"]
  LED8 = LED - 5mm [color="Yellow (595nm)" current=0.030 package="5 mm [THT]"]
  LED9 = LED - 5mm [color="Yellow (595nm)" current=0.030 package="5 mm [THT]"]
  LED10 = LED - 5mm [color="Yellow (595nm)" current=0.030 package="5 mm [THT]"]
  LED11 = LED - 5mm [color="Green (560nm)" current=0.030 package="5 mm [THT]"]
  LED12 = LED - 5mm [color="Green (560nm)" current=0.030 package="5 mm [THT]"]
  LED13 = LED - 5mm [color="Green (560nm)" current=0.030 package="5 mm [THT]"]
  LED14 = LED - 5mm [color="Blue (430nm)" current=0.030 package="5 mm [THT]"]
  LED15 = LED - 5mm [color="Blue (430nm)" current=0.030 package="5 mm [THT]"]
  LED16 = LED - 5mm [color="Blue (430nm)" current=0.030 package="5 mm [THT]"]
  WeMos_D1_Mini1 = WeMos D1 Mini

nets:
  GND: U2.GND, U2.OE, U3.GND, U3.OE, WeMos_D1_Mini1.G
  VCC: U2.MR, U2.VCC, U3.MR, U3.VCC, WeMos_D1_Mini1.5V
  N1: U2.SH_CP, U3.SH_CP, WeMos_D1_Mini1.D5
  N2: U2.ST_CP, U3.ST_CP, WeMos_D1_Mini1.D8
  N3: U2.DS, U3.Q7'
  N4: U3.DS, WeMos_D1_Mini1.D7
  N5: LED1.cathode, R1.Pin_0
  N6: R1.Pin_1, R2.Pin_1, R3.Pin_1, R4.Pin_1, R5.Pin_1, R6.Pin_1, R7.Pin_1, R8.Pin_1, R9.Pin_1, R10.Pin_1, R11.Pin_1, R12.Pin_1, R13.Pin_1, R14.Pin_1, R15.Pin_1, R16.Pin_1
  N7: R2.Pin_0, LED2.cathode
  N8: R3.Pin_0, LED3.cathode
  N9: R4.Pin_0, LED4.cathode
  N10: R5.Pin_0, LED5.cathode
  N11: R6.Pin_0, LED6.cathode
  N12: R7.Pin_0, LED7.cathode
  N13: R8.Pin_0, LED8.cathode
  N14: R9.Pin_0, LED9.cathode
  N15: R10.Pin_0, LED10.cathode
  N16: R11.Pin_0, LED11.cathode
  N17: R12.Pin_0, LED12.cathode
  N18: R13.Pin_0, LED13.cathode
  N19: R14.Pin_0, LED14.cathode
  N20: R15.Pin_0, LED15.cathode
  N21: R16.Pin_0, LED16.cathode
