# Fritzing sketch single_reset_s (saved by Fritzing 1.0.1rc)
breadboards: 1

parts:
  WeMos_D1_Mini1 = WeMos D1 Mini
  S3 = Pushbutton [package="[THT]"]
  Q1 = TRANSISTOR_NPN [package=to-92]
  C2 = Electrolytic Capacitor [capacitance=0.47µF voltage=6.3V package="100 mil [THT, electrolytic]"]
  R2 = Resistor [tolerance=±5% power=0.25 resistance=220 package=THT]
  R3 = Resistor [tolerance=±5% power=0.25 resistance=220 package=THT]

nets:
  N1: WeMos_D1_Mini1.3V3, S3.Pin_3, S3.Pin_4
  N2: WeMos_D1_Mini1.D1, R3.Pin_0
  N3: WeMos_D1_Mini1.G, Q1.E
  N4: WeMos_D1_Mini1.RST, C2.+
  N5: S3.Pin_1, S3.Pin_2, R2.Pin_0
  N6: Q1.B, R2.Pin_1
  N7: Q1.C, C2.-, R3.Pin_1
