# Fritzing sketch HC-06_connection (saved by Fritzing 0.9.6b)
breadboards: 1

parts:
  Деталь2 = Bluetooth HC-05 Macho  # not connected
  Деталь4 = Arduino Nano (Rev3.0)
  Деталь5 = Logic Level Converter

nets:
  GND: Деталь4.GND, Деталь5.GND
  N1: Деталь4.D10, Деталь5.RX_HV
  N2: Деталь4.D11/MOSI, Деталь5.TX_HV
  N3: Деталь4.5V, Деталь5.HV
  N4: Деталь4.3V3, Деталь5.LV
